# Fritzing sketch LFn-t Sketch (saved by Fritzing 0.9.3b)
breadboards: 1

parts:
  Part1 = Arduino Uno (Rev3) - ICSP
  LCM1602_IIC1 = LCM1602 IIC [part_number="LCM1602 IIC" chip_label="LCM1602 IIC" package="DIP (Dual Inline) [THT]"]
  LCD1 = LCD screen
  LED3 = LED - 5mm [color="Blue (470nm)" package="5 mm [THT]"]
  LED4 = LED - 5mm [color="Yellow (585nm)" package="5 mm [THT]"]
  LED5 = LED - 5mm [color="Red (633nm)" package="5 mm [THT]"]
  LED6 = LED - 5mm [color="Green (555nm)" package="5 mm [THT]"]
  LED7 = LED - 5mm [color="Blue (470nm)" package="5 mm [THT]"]
  LED8 = LED - 5mm [color="Yellow (585nm)" package="5 mm [THT]"]
  S1 = Momentary Switch 6mm 2pin
  S2 = Momentary Switch 6mm 2pin
  S3 = Momentary Switch 6mm 2pin
  S4 = Momentary Switch 6mm 2pin
  S5 = Momentary Switch 6mm 2pin
  S6 = Momentary Switch 6mm 2pin
  S7 = Momentary Switch 6mm 2pin
  S8 = Momentary Switch 6mm 2pin
  LED1 = LED - 5mm [color="Red (633nm)" package="5 mm [THT]"]
  LED2 = LED - 5mm [color="Green (555nm)" package="5 mm [THT]"]
  R2 = Resistor [tolerance=±5% resistance=220 package=THT]
  R5 = Resistor [tolerance=±5% resistance=220 package=THT]
  R6 = Resistor [tolerance=±5% resistance=220 package=THT]
  R7 = Resistor [tolerance=±5% resistance=220 package=THT]
  R8 = Resistor [tolerance=±5% resistance=220 package=THT]
  R9 = Resistor [tolerance=±5% resistance=220 package=THT]
  R10 = Resistor [tolerance=±5% resistance=100 package=THT]
  R11 = Resistor [tolerance=±5% resistance=100 package=THT]

nets:
  N1: Part1.A4/SDA, LCM1602_IIC1.SDA
  N2: Part1.A5/SCL, LCM1602_IIC1.SCL
  N3: Part1.ICSP_MOSI, Part1.D11_PWM/MOSI, R2.Pin_1, R8.Pin_1
  N4: Part1.D8, S7.1
  N5: Part1.D9_PWM, S8.1
  N6: Part1.D10_PWM/SS, R5.Pin_1, R7.Pin_1
  N7: Part1.D12/MISO, R10.Pin_1, R11.Pin_1
  N8: Part1.D13/SCK, R6.Pin_1, R9.Pin_1
  N9: Part1.D2, S1.1
  N10: Part1.D3_PWM, S2.1
  N11: Part1.D4, S3.1
  N12: Part1.D5_PWM, S4.1
  N13: Part1.D6_PWM, S5.1
  N14: Part1.D7, S6.1
  5V: Part1.5V, LCM1602_IIC1.VCC
  GND: Part1.GND, LCM1602_IIC1.GND, LED3.cathode, LED4.cathode, LED5.cathode, LED6.cathode, LED7.cathode, LED8.cathode, S1.2, S2.2, S3.2, S4.2, S5.2, S6.2, S7.2, S8.2, LED1.cathode, LED2.cathode
  VSS: LCM1602_IIC1.VSS, LCD1.VSS
  VDD: LCM1602_IIC1.VDD, LCD1.VDD
  N15: LCM1602_IIC1.V0, LCD1.V0
  N16: LCM1602_IIC1.RS, LCD1.RS
  N17: LCM1602_IIC1.RW, LCD1.R/W
  N18: LCM1602_IIC1.E, LCD1.E
  N19: LCM1602_IIC1.D0, LCD1.DB0
  N20: LCM1602_IIC1.D1, LCD1.DB1
  N21: LCM1602_IIC1.D2, LCD1.DB2
  N22: LCM1602_IIC1.D3, LCD1.DB3
  N23: LCM1602_IIC1.D4, LCD1.DB4
  N24: LCM1602_IIC1.D5, LCD1.DB5
  N25: LCM1602_IIC1.D6, LCD1.DB6
  N26: LCM1602_IIC1.D7, LCD1.DB7
  N27: LCM1602_IIC1.A, LCD1.LED+
  N28: LCM1602_IIC1.K, LCD1.LED-
  N29: LED3.anode, R10.Pin_0
  N30: LED4.anode, R6.Pin_0
  N31: LED5.anode, R7.Pin_0
  N32: LED6.anode, R8.Pin_0
  N33: LED7.anode, R11.Pin_0
  N34: LED8.anode, R9.Pin_0
  N35: LED1.anode, R5.Pin_0
  N36: LED2.anode, R2.Pin_0

custom parts:
  LCM1602 IIC: I2C-Module to use a 1602 or 2004 LCD on with the wire.h libory Serial LCD Modul
  Momentary Switch 6mm 2pin: Momentary Switch 6mm 2 pin Button commonly used for reset or general input.
